# Fritzing sketch LeapMotionRC (saved by Fritzing 0.8.5b)
breadboards: 1

parts:
  Parte1 = Arduino Uno (Rev3)
  R1 = Resistor [tolerance=±5% resistance=330 package=THT]
  R2 = Resistor [tolerance=±5% resistance=330 package=THT]
  R3 = Resistor [tolerance=±5% resistance=330 package=THT]
  R4 = Resistor [tolerance=±5% resistance=330 package=THT]
  LED1 = LED - 5mm [color="Red (633nm)" package="5 mm [THT]"]
  LED2 = LED - 5mm [color="Green (560nm)" package="5 mm [THT]"]
  LED4 = LED - 5mm [color="Blue (470nm)" package="5 mm [THT]"]
  J1 = female pin header, 4 pins [form="♀ (female)"]
  Q1 = NPN-Transistor [part_number=2N2222 package="TO92 [THT]"]
  Q2 = NPN-Transistor [part_number=2N2222 package="TO92 [THT]"]
  Q3 = NPN-Transistor [part_number=2N2222 package="TO92 [THT]"]
  Q4 = NPN-Transistor [part_number=2N2222 package="TO92 [THT]"]
  R5 = Resistor [tolerance=±5% resistance=10k package=THT]
  R6 = Resistor [tolerance=±5% resistance=10k package=THT]
  R7 = Resistor [tolerance=±5% resistance=10k package=THT]
  R8 = Resistor [tolerance=±5% resistance=10k package=THT]
  LED3 = LED - 5mm [color="Yellow (585nm)" package="5 mm [THT]"]

nets:
  N1: Parte1.D8, R3.Pin_0, R5.Pin_0
  N2: Parte1.D9_PWM, R4.Pin_0, R6.Pin_0
  N3: Parte1.D10_PWM/SS, R1.Pin_0, R7.Pin_0
  N4: Parte1.D11_PWM/MOSI, R2.Pin_0, R8.Pin_0
  N5: Parte1.GND, LED1.anode, LED2.anode, LED4.anode, Q1.E, Q2.E, Q3.E, Q4.E, LED3.anode
  N6: R1.Pin_1, LED3.cathode
  N7: R2.Pin_1, LED4.cathode
  N8: R3.Pin_1, LED1.cathode
  N9: R4.Pin_1, LED2.cathode
  N10: J1.pin1, Q2.C
  N11: J1.pin2, Q1.C
  N12: J1.pin3, Q3.C
  N13: J1.pin4, Q4.C
  N14: Q1.B, R7.Pin_1
  N15: Q2.B, R8.Pin_1
  N16: Q3.B, R6.Pin_1
  N17: Q4.B, R5.Pin_1

notes:
  F B L R
